# Fritzing sketch Automated irrigation circuit (saved by Fritzing 0.9.4)

parts:
  Part1 = Arduino Uno (Rev3)
  Part2 = LCD1602-I2C
  Part3 = Soil Moisture Sensor
  LED1 = LEDs [package=led10mm]
  KY-1 = Keyes Relay [package=THT]
  Power_plug1 = Power plug

nets:
  N1: Part1.A0, Part3.SIG
  N2: Part1.A4/SDA, Part2.VCC
  N3: Part1.A5/SCL, Part2.GND
  N4: Part1.D13/SCK, KY-1.signal
  GND: Part1.GND, Part2.SCL, Part3.GND, KY-1.ground
  5V: Part1.5V, Part2.SDA, Part3.VCC, KY-1.power
  N5: LED1.A, Power_plug1.VCC
  N6: LED1.C, KY-1.NO
  N7: KY-1.C, Power_plug1.GND

custom parts:
  LCD1602-I2C: A standard character display, usually with 2x16 characters. Comes in many colors with LCM1602 IIC attached.
  LEDs: LEDs Standard schematic elements and footprints for 5mm, 3mm, 1206, and 0603 sized LEDs. 5mm - Spark Fun Electronics SKU : COM-00529 (and others)
  Keyes Relay: The Keyes 5V relay module is suitable for SCM development, home appliance control. It uses a 5V~12V TIL control signal which can control DC / AC signal.
